// Digital circuit CPU.dig as structural Verilog
module CPU (
  input  clock
);

  wire [1:0] multiplexer_1_out;
  wire [6:0] MainControl_d;
  wire [15:0] bitextender_1_out, instructionReg_d, multiplexer_2_out, pc_incrementer_r, programCounter_q,
       reg_file_p4, reg_file_p7, reg_file_p8;

  D_FF #(.Bits(16)) programCounter (.D(pc_incrementer_r), .C(~clock), .Q(programCounter_q));  // open: nQ
  ALU pc_incrementer (.r(pc_incrementer_r), .a(programCounter_q), .b(16'h2), .s(4'b0010));  // open: zero, overflow
  ROM #(.AddrBits(16), .Bits(16)) instructionReg (.A(programCounter_q), .sel(1'b1), .D(instructionReg_d));
  Multiplexer #(.Bits(2)) multiplexer_1 (
    .sel(MainControl_d[6]), .in_0(instructionReg_d[9:8]), .in_1(instructionReg_d[7:6]),
    .out(multiplexer_1_out));
  ROM #(.AddrBits(4), .Bits(7)) MainControl (.A(instructionReg_d[15:12]), .sel(1'b1), .D(MainControl_d));
  // reg_file reg_file: pin names not known; wires that end beside it: instructionReg_d[11:10], instructionReg_d[9:8], multiplexer_1_out, reg_file_p4, MainControl_d[4], clock, reg_file_p7, reg_file_p8
  BitExtender bitextender_1 (.in(instructionReg_d[7:0]), .out(bitextender_1_out));
  Multiplexer #(.Bits(16)) multiplexer_2 (
    .sel(MainControl_d[5]), .in_0(reg_file_p8), .in_1(bitextender_1_out), .out(multiplexer_2_out));
  ALU execution_unit (
    .r(reg_file_p4), .a(reg_file_p7), .b(multiplexer_2_out), .s(MainControl_d[3:0]));  // open: zero, overflow

  // Notes on the sheet:
  //   contents of MainControl (hex, n*v repeats v):
  //   52,56,50,51,5c,5d,57,32
  //   RegDest
  //   ALUsrc
  //   RegWrite
  //   ALUOp
endmodule
